# Fritzing sketch hygienotronics_status_dashboard (saved by Fritzing 0.7.3b)
breadboards: 1

parts:
  Arduino1 = Arduino
  R1 = Resistor [tolerance=±5% resistance=220 package=THT]
  LED1 = LED - 5mm [color="Yellow (595nm)" package="5 mm [THT]"]
  R2 = Resistor [tolerance=±5% resistance=220 package=THT]
  R3 = Resistor [tolerance=±5% resistance=220 package=THT]
  R4 = Resistor [tolerance=±5% resistance=220 package=THT]
  LED2 = LED - 5mm [color="Red (660nm)" package="5 mm [THT]"]
  LED3 = LED - 5mm [color="Red (660nm)" package="5 mm [THT]"]
  LED4 = LED - 5mm [color="Yellow (595nm)" package="5 mm [THT]"]
  R5 = Resistor [tolerance=±5% resistance=220 package=THT]
  R6 = Resistor [tolerance=±5% resistance=220 package=THT]
  LED5 = LED - 5mm [color="Green (570nm)" package="5 mm [THT]"]
  LED6 = LED - 5mm [color="Green (570nm)" package="5 mm [THT]"]

nets:
  N1: Arduino1.GND, LED3.cathode, LED4.cathode, LED6.cathode
  N2: Arduino1.D13, R4.Pin_1
  N3: Arduino1.D12, R3.Pin_1
  N4: Arduino1.D11, R6.Pin_1
  N5: Arduino1.D10, R5.Pin_1
  N6: Arduino1.D9, R2.Pin_1
  N7: Arduino1.D8, R1.Pin_1
  N8: R1.Pin_0, LED1.anode
  N9: LED1.cathode, LED2.cathode, LED5.cathode
  N10: R2.Pin_0, LED2.anode
  N11: R3.Pin_0, LED3.anode
  N12: R4.Pin_0, LED4.anode
  N13: R5.Pin_0, LED5.anode
  N14: R6.Pin_0, LED6.anode

notes:
  T Status
  W Status
  Hygienotronics Dashboard
  listen
  trigger
  +
